# Fritzing sketch esquema (saved by Fritzing 0.9.3b)
breadboards: 1

parts:
  R1 = Photocell (LDR) [package=THT]
  R2 = Resistor [tolerance=±5% resistance=10k package="2010 [SMD]"]
  Componente2 = Arduino Uno (Rev3) - ICSP
  BAT1 = BC9VPC [package=bc9vpc]
  M1 = DC Motor
  L298N2 = L298N DC motor driver
  hc-sr1 = hc-sr04
  LCD2 = LCD screen
  LCM1602_IIC2 = LCM1602 IIC [part_number="LCM1602 IIC" chip_label="LCM1602 IIC" package="DIP (Dual Inline) [THT]"]
  S2 = Momentary Switch [package=ksa_sealed_tac_switch]
  S3 = Momentary Switch [package=ksa_sealed_tac_switch]
  S4 = Momentary Switch [package=ksa_sealed_tac_switch]
  R3 = Resistor [tolerance=±5% resistance=10k package="2010 [SMD]"]
  R4 = Resistor [tolerance=±5% resistance=10k package="2010 [SMD]"]
  R5 = Resistor [tolerance=±5% resistance=10k package="2010 [SMD]"]

nets:
  N1: R1.pin_0, R2.Pin_1
  N2: R1.pin_1, Componente2.A0
  GND: R2.Pin_0, Componente2.GND, L298N2.GND, hc-sr1.GND, LCM1602_IIC2.GND, R3.Pin_0, R4.Pin_0, R5.Pin_0
  N3: Componente2.A4/SDA, LCM1602_IIC2.SDA
  N4: Componente2.A5/SCL, LCM1602_IIC2.SCL
  N5: Componente2.D11_PWM/MOSI, hc-sr1.Trig
  N6: Componente2.D12/MISO, hc-sr1.Echo
  N7: Componente2.D2, S2.4, R3.Pin_1
  N8: Componente2.D3_PWM, S3.4, R4.Pin_1
  N9: Componente2.D4, S4.4, R5.Pin_1
  N10: Componente2.D5_PWM, L298N2.ENB
  N11: Componente2.D6_PWM, L298N2.IN4
  N12: Componente2.D7, L298N2.IN3
  VCC: Componente2.5V, hc-sr1.VCC, LCM1602_IIC2.VCC, S2.2, S3.2, S4.2
  N13: BAT1.V+, L298N2.12V
  N14: BAT1.V-, L298N2.5V
  N15: M1.pin_1, L298N2.OUT4
  N16: M1.pin_2, L298N2.OUT3
  VSS: LCD2.VSS, LCM1602_IIC2.VSS
  VDD: LCD2.VDD, LCM1602_IIC2.VDD
  N17: LCD2.V0, LCM1602_IIC2.V0
  N18: LCD2.RS, LCM1602_IIC2.RS
  N19: LCD2.R/W, LCM1602_IIC2.RW
  N20: LCD2.E, LCM1602_IIC2.E
  N21: LCD2.DB0, LCM1602_IIC2.D0
  N22: LCD2.DB1, LCM1602_IIC2.D1
  N23: LCD2.DB2, LCM1602_IIC2.D2
  N24: LCD2.DB3, LCM1602_IIC2.D3
  N25: LCD2.DB4, LCM1602_IIC2.D4
  N26: LCD2.DB5, LCM1602_IIC2.D5
  N27: LCD2.DB6, LCM1602_IIC2.D6
  N28: LCD2.DB7, LCM1602_IIC2.D7
  N29: LCD2.LED+, LCM1602_IIC2.A
  N30: LCD2.LED-, LCM1602_IIC2.K
  N31: LCM1602_IIC2.LED_A, LCM1602_IIC2.LED_B

custom parts:
  L298N DC motor driver: 2x DC motor driver with 78M05 positive voltage regulator (7..35 V) L298N: max 46 V, 2 A Set 5 V Enable jumper to enable 5 V regultor (needed for the L298N) and +5 V output at screw terminal or supply external +5 V at screw terminal Set ENA and/or ENB to +5 V to enable motor permanently or supply ENA and/or ENB with PWM signal IN1 and IN2 set rotation directory for motor A (OUT1/OUT2) IN2 and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
  LCM1602 IIC: I2C-Module to use a 1602 or 2004 LCD on with the wire.h libory Serial LCD Modul
